// Logisim project CAO Group 12.circ as structural Verilog: 1 circuit, main circuit main
module main (
  input  in_1
);

  wire button_1_out, Clear_out, clock_1_out, d_ff_1_q, d_ff_1_qn, d_ff_2_q, d_ff_2_qn, iLoad_out, not_1_out,
       or_1_out, or_2_out, Out_out;

  LED led_1 (.in(in_1));
  not not_1 (not_1_out, in_1);
  LED led_2 (.in(not_1_out));
  or or_1 (or_1_out, not_1_out, d_ff_2_q);
  or or_2 (or_2_out, d_ff_1_q, d_ff_2_qn);
  Button button_1 (.out(button_1_out));
  Clock clock_1 (.out(clock_1_out));
  D_Flip_Flop d_ff_1 (
    .clk(clock_1_out), .D(or_1_out), .Q(d_ff_1_q), .Qn(d_ff_1_qn), .reset(button_1_out));  // open: preset, en
  D_Flip_Flop d_ff_2 (
    .clk(clock_1_out), .D(or_2_out), .Q(d_ff_2_q), .Qn(d_ff_2_qn), .reset(button_1_out));  // open: preset, en
  and iLoad (iLoad_out, d_ff_2_q, d_ff_1_qn);
  and Clear (Clear_out, d_ff_1_qn, d_ff_2_qn);
  and Out (Out_out, d_ff_1_q, d_ff_2_qn);
  LED led_3 (.in(iLoad_out));
  LED led_4 (.in(Clear_out));
  LED led_5 (.in(Out_out));

  // Notes on the sheet:
  //   INPUT from Condition
  //   D1
  //   D0
endmodule
